# Fritzing sketch Diagrama_Simple (saved by Fritzing 0.9.3b)
breadboards: 1

parts:
  IC1 = AD8232 HeartRate Monitor [part_number=SEN-12650 chip_label=IC package="DIP (Dual Inline) [THT]"]
  Componente1 = Arduino Uno (Rev3)

nets:
  GND: IC1.GND, Componente1.GND
  3.3V: IC1.3.3v, Componente1.AREF, Componente1.3V3
  N1: IC1.OUTPUT, Componente1.A0
  N2: IC1.LO-, Componente1.D7
  N3: IC1.LO+, Componente1.D6_PWM

custom parts:
  AD8232 HeartRate Monitor: A DIP stand-in part for whatever IC you want. With 10 pins on a 600mil dual inline package (DIP) footprint.
